# Fritzing sketch Esquema_compacto (saved by Fritzing 0.9.6b)
breadboards: 1

parts:
  LCD1 = LCD screen
  U1 = IC, DIP package, 8 pins [chip_label=PCF8583]
  RHT1 = Humidity and Temperature Sensor RHT03
  Componente1 = Adafruit Feather 32u4 Basic Proto [part_number="Adafruit #2771"]
  S4 = Pushbutton [package="[THT]"]
  S5 = Pushbutton [package="[THT]"]
  R1 = Resistor [tolerance=±5% resistance=10k package="1206 [SMD]"]
  R2 = Resistor [tolerance=±5% resistance=10k package="1206 [SMD]"]
  R3 = Resistor [tolerance=±5% resistance=10k package="1206 [SMD]"]
  R5 = Resistor [tolerance=±5% resistance=100k package="1206 [SMD]"]
  Y1 = CRYSTAL [part_number=32.768Mhz package=crystal-32khz-smd_epson_mc146]
  C1 = Capacitor [part_number=25uF package=cap-pth-small2]
  R4 = Resistor [tolerance=±5% resistance=100k power=0.25 package=THT]

nets:
  GND: LCD1.VSS, LCD1.V0, LCD1.R/W, LCD1.DB0, LCD1.DB1, LCD1.DB2, LCD1.DB3, U1.pin3, U1.pin4, RHT1.GND_2, Componente1.GND, R1.Pin_1, R2.Pin_1, R5.Pin_0
  5V: LCD1.VDD, Componente1.VBAT, R4.Pin_1
  N1: LCD1.RS, Componente1.A1
  N2: LCD1.E, Componente1.A0
  N3: LCD1.DB4, Componente1.A2
  N4: LCD1.DB5, Componente1.A3
  N5: LCD1.DB6, Componente1.A4
  N6: LCD1.DB7, Componente1.A5
  N7: U1.pin1, Y1.2, C1.1
  N8: U1.pin2, Y1.1
  N9: U1.pin5, Componente1.2
  N10: U1.pin6, Componente1.3
  3.3V: U1.pin8, S4.Pin_1, S4.Pin_2, S5.Pin_1, S5.Pin_2, C1.2
  N11: RHT1.Vcc, Componente1.6, R3.Pin_0
  N12: RHT1.Data-signal, Componente1.9, R3.Pin_1
  N13: Componente1.1, S5.Pin_3, S5.Pin_4, R1.Pin_0
  N14: Componente1.0, S4.Pin_3, S4.Pin_4, R2.Pin_0
  N15: Componente1.10, R5.Pin_1, R4.Pin_0

custom parts:
  Adafruit Feather 32u4 Basic Proto: At the Feather 32u4's heart is at ATmega32u4 clocked at 8 MHz and at 3.3V logic, a chip setup we've had tons of experience with as it's the same as the Flora. This chip has 32K of flash and 2K of RAM, with built in USB so not only does it have a USB-to-Serial program & debug capability built in with no need for an FTDI-like chip, it can also act like a mouse, keyboard, USB MIDI device, etc.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
